// Logisim project Assignment_1.circ as structural Verilog: 1 circuit, main circuit main
module main (
  input  Armed,
  input  Door,
  input  Glass,
  input  Motion,
  output Alarm
);

  wire or_1_out, or_2_out;

  or or_1 (or_1_out, Door, Glass);
  or or_2 (or_2_out, or_1_out, Motion);
  and and_1 (Alarm, Armed, or_2_out);
endmodule
