// Logisim project Assignment_2.circ as structural Verilog: 1 circuit, main circuit main
module main (
  input  A,
  input  B,
  input  C,
  output X
);

  wire and_1_out, and_2_out, not_1_out, not_2_out;

  not not_1 (not_1_out, A);
  not not_2 (not_2_out, B);
  and and_1 (and_1_out, not_1_out, B, C);
  and and_2 (and_2_out, C, not_2_out, A);
  or or_1 (X, and_1_out, and_2_out);
endmodule
