// Logisim project NAND_XOR.circ as structural Verilog: 1 circuit, main circuit main
module main (
  input  X,
  input  Y,
  output Z
);

  wire nand_1_out, nand_2_out, nand_3_out;

  nand nand_1 (nand_1_out, X, Y);
  nand nand_2 (nand_2_out, X, nand_1_out);
  nand nand_3 (nand_3_out, nand_1_out, Y);
  nand nand_4 (Z, nand_2_out, nand_3_out);
endmodule
