// Logisim project xorGate1.circ as structural Verilog: 1 circuit, main circuit main
module main (
  input  X,
  input  Y,
  output Z
);

  wire and_1_out, not_1_out, or_1_out;

  or or_1 (or_1_out, X, Y);
  and and_1 (and_1_out, X, Y);
  not not_1 (not_1_out, and_1_out);
  and and_2 (Z, or_1_out, not_1_out);
endmodule
