// Logisim project second.circ as structural Verilog: 1 circuit, main circuit main
module main (
  input  A1,
  input  B1,
  input  A2,
  input  B2,
  input  A3,
  input  B3,
  input  A4,
  input  B4,
  output S1,
  output S2,
  output S3,
  output S4,
  output C4
);

  wire and_1_out, and_2_out, and_3_out, and_4_out, and_5_out, and_6_out, and_7_out, and_8_out, not_1_out,
       not_2_out, not_3_out, not_4_out, or_1_out, or_2_out, or_3_out, xor_1_out, xor_2_out, xor_3_out,
       xor_4_out;

  not not_1 (not_1_out, B1);
  not not_2 (not_2_out, B2);
  not not_3 (not_3_out, B3);
  not not_4 (not_4_out, B4);
  xor xor_1 (xor_1_out, A1, not_1_out);
  and and_1 (and_1_out, not_1_out, A1);
  xor xor_2 (xor_2_out, A2, not_2_out);
  and and_2 (and_2_out, not_2_out, A2);
  xor xor_3 (xor_3_out, A3, not_3_out);
  and and_3 (and_3_out, not_3_out, A3);
  xor xor_4 (xor_4_out, A4, not_4_out);
  and and_4 (and_4_out, not_4_out, A4);
  xor xor_5 (S1, xor_1_out, 1'b1);
  and and_5 (and_5_out, 1'b1, xor_1_out);
  xor xor_6 (S2, xor_2_out, or_1_out);
  and and_6 (and_6_out, or_1_out, xor_2_out);
  xor xor_7 (S3, xor_3_out, or_2_out);
  and and_7 (and_7_out, or_2_out, xor_3_out);
  xor xor_8 (S4, xor_4_out, or_3_out);
  and and_8 (and_8_out, or_3_out, xor_4_out);
  or or_1 (or_1_out, and_5_out, and_1_out);
  or or_2 (or_2_out, and_6_out, and_2_out);
  or or_3 (or_3_out, and_7_out, and_3_out);
  or or_4 (C4, and_8_out, and_4_out);
endmodule
