// Logisim project 4bitALURegister.circ as structural Verilog: 1 circuit, main circuit main
module main (
  input  [1:0] in_1,
  input  D0,
  input  D1,
  input  D2,
  input  D3,
  input  Control,
  input  in_7,
  input  in_8,
  input  in_9,
  input  in_10,
  input  in_11,
  output [3:0] out_12,
  output Q0,
  output Q1,
  output Q2,
  output Q3,
  output out_17,
  output out_18,
  output out_19,
  output out_20
);

  wire CLK_out, clock_1_out;
  wire [3:0] adder_1_out, and_1_out, or_1_out, subtractor_1_out;

  Clock clock_1 (.out(clock_1_out));
  D_Flip_Flop d_ff_1 (.D(D0), .clk(CLK_out), .Q(Q0), .reset(Control));  // open: Qn, preset
  Clock CLK (.out(CLK_out));
  D_Flip_Flop d_ff_2 (.D(in_7), .clk(clock_1_out), .Q(out_17), .reset(in_11));  // open: Qn, preset
  D_Flip_Flop d_ff_3 (.D(D1), .clk(CLK_out), .Q(Q1), .reset(Control));  // open: Qn, preset
  D_Flip_Flop d_ff_4 (.D(in_8), .clk(clock_1_out), .Q(out_18), .reset(in_11));  // open: Qn, preset
  D_Flip_Flop d_ff_5 (.D(D2), .clk(CLK_out), .Q(Q2), .reset(Control));  // open: Qn, preset
  D_Flip_Flop d_ff_6 (.D(in_9), .clk(clock_1_out), .Q(out_19), .reset(in_11));  // open: Qn, preset
  D_Flip_Flop d_ff_7 (.D(D3), .clk(CLK_out), .Q(Q3), .reset(Control));  // open: Qn, preset
  D_Flip_Flop d_ff_8 (.D(in_10), .clk(clock_1_out), .Q(out_20), .reset(in_11));  // open: Qn, preset
  Adder #(.width(4)) adder_1 (
    .a({out_20, out_19, out_18, out_17}), .b({Q3, Q2, Q1, Q0}), .out(adder_1_out));  // open: cin, cout
  Subtractor #(.width(4)) subtractor_1 (
    .a({out_20, out_19, out_18, out_17}), .b({Q3, Q2, Q1, Q0}), .out(subtractor_1_out));  // open: bin, bout
  assign and_1_out = {out_20, out_19, out_18, out_17} & {Q3, Q2, Q1, Q0};  // AND_Gate and_1, 4 bits wide
  assign or_1_out = {out_20, out_19, out_18, out_17} | {Q3, Q2, Q1, Q0};  // OR_Gate or_1, 4 bits wide
  Multiplexer #(.select(2), .width(4)) multiplexer_1 (
    .in0(adder_1_out), .in1(subtractor_1_out), .in2(and_1_out), .in3(or_1_out), .out(out_12), .sel(in_1));
endmodule
