// Logisim project 4bitregister.circ as structural Verilog: 1 circuit, main circuit main
module main (
  input  D0,
  input  D1,
  input  D2,
  input  D3,
  input  Control,
  output Q0,
  output Q1,
  output Q2,
  output Q3,
  output out_10
);

  wire CLK_out;

  Clock CLK (.out(CLK_out));
  D_Flip_Flop d_ff_1 (.D(D0), .clk(CLK_out), .Q(Q0), .reset(Control));  // open: Qn, preset
  D_Flip_Flop d_ff_2 (.D(D1), .clk(CLK_out), .Q(Q1), .reset(Control));  // open: Qn, preset
  D_Flip_Flop d_ff_3 (.D(D2), .clk(CLK_out), .Q(Q2), .reset(Control));  // open: Qn, preset
  D_Flip_Flop d_ff_4 (.D(D3), .clk(CLK_out), .Q(Q3), .reset(Control));  // open: Qn, preset
endmodule
